// Logisim project andgateSim.circ as structural Verilog: 1 circuit, main circuit main
module main (
  input  in_1,
  input  b,
  output out_3
);

  and and_1 (out_3, in_1, b);

  // Notes on the sheet:
  //   a
  //   AND GATE
  //   x
endmodule
