// Logisim project fulladderSim.circ as structural Verilog: 1 circuit, main circuit main
module main (
  input  in_1,
  input  in_2,
  input  c,
  output out_4,
  output out_5
);

  wire and_1_out, and_2_out, and_3_out, and_4_out, and_5_out, and_6_out, not_1_out, not_2_out, not_3_out,
       not_4_out, or_1_out;

  not not_1 (not_1_out, in_1);
  not not_2 (not_2_out, in_2);
  and and_1 (and_1_out, not_1_out, in_2);
  and and_2 (and_2_out, not_2_out, in_1);
  or or_1 (or_1_out, and_1_out, and_2_out);
  and and_3 (and_3_out, or_1_out, c);
  and and_4 (and_4_out, in_1, in_2);
  not not_3 (not_3_out, or_1_out);
  not not_4 (not_4_out, c);
  and and_5 (and_5_out, c, not_3_out);
  and and_6 (and_6_out, or_1_out, not_4_out);
  or or_2 (out_4, and_5_out, and_6_out);
  or or_3 (out_5, and_3_out, and_4_out);

  // Notes on the sheet:
  //   a
  //   b
  //   FULL ADDER CIRCUIT
  //   a xor b
  //   (a xor b). c
  //   a.b
  //   Sum(x)
  //   Carry(y)
endmodule
