// Logisim project halfadder_ckt.circ as structural Verilog: 1 circuit, main circuit main
module main (
  input  in_1,
  input  in_2,
  output out_3,
  output Carry_y
);

  wire and_1_out, and_2_out, not_1_out, not_2_out;

  not not_1 (not_1_out, in_1);
  not not_2 (not_2_out, in_2);
  and and_1 (and_1_out, not_1_out, in_2);
  and and_2 (and_2_out, not_2_out, in_1);
  and and_3 (Carry_y, in_1, in_2);
  or or_1 (out_3, and_1_out, and_2_out);

  // Notes on the sheet:
  //   a
  //   b
  //   HALF ADDER CIRCUIT
  //   Sum(x)
endmodule
