// Logisim project nandgateSim.circ as structural Verilog: 1 circuit, main circuit main
module main (
  input  in_1,
  input  y,
  output out_3
);

  wire and_1_out;

  and and_1 (and_1_out, in_1, y);
  not not_1 (out_3, and_1_out);

  // Notes on the sheet:
  //   x
  //   NAND GATE
endmodule
