// Logisim project norgateSim.circ as structural Verilog: 1 circuit, main circuit main
module main (
  input  in_1,
  input  y,
  output out_3
);

  wire or_1_out;

  or or_1 (or_1_out, in_1, y);
  not not_1 (out_3, or_1_out);

  // Notes on the sheet:
  //   x
  //   NOR GATE
endmodule
